# Fritzing sketch Dashboard (saved by Fritzing 0.8.5b)
breadboards: 1

parts:
  Raspberry_Pi_B_rev1 = Raspberry Pi B rev2
  LCD1 = LCD screen
  LED1 = LED - 5mm [color="Red (633nm)" package="5 mm [THT]"]
  J1 = Basic Servo  # not connected
  LED2 = LED - 5mm [color="Red (633nm)" package="5 mm [THT]"]  # not connected
  LED3 = LED - 5mm [color="Red (633nm)" package="5 mm [THT]"]
  S1 = Pushbutton [package="[THT]"]
  S2 = Pushbutton [package="[THT]"]
  S3 = Pushbutton [package=THT]  # not connected
  S4 = Pushbutton [package=THT]  # not connected
  J2 = Piezo Speaker  # not connected
  S5 = Pushbutton [package=THT]  # not connected
  S6 = Pushbutton [package=THT]  # not connected

nets:
  3V3: Raspberry_Pi_B_rev1.3V3, Raspberry_Pi_B_rev1.5V, Raspberry_Pi_B_rev1.GPIO_24, LCD1.VDD, LCD1.R/W, LCD1.LED+
  GND: Raspberry_Pi_B_rev1.GPIO_3, Raspberry_Pi_B_rev1.GND, Raspberry_Pi_B_rev1.GPIO_7, LCD1.VSS, LCD1.DB5, LCD1.DB6, LCD1.LED-, LED1.anode, LED3.anode
  N1: Raspberry_Pi_B_rev1.GPIO_23, Raspberry_Pi_B_rev1.GPIO_22, LCD1.RS
  N2: Raspberry_Pi_B_rev1.GPIO_17, Raspberry_Pi_B_rev1.GPIO_18, LCD1.V0
  N3: Raspberry_Pi_B_rev1.GPIO_9, Raspberry_Pi_B_rev1.GPIO_25, LCD1.E
  N4: Raspberry_Pi_B_rev1.GPIO_11, Raspberry_Pi_B_rev1.GPIO_8, LCD1.DB4
  N5: S1.Pin_1, S1.Pin_2
  N6: S1.Pin_3, S1.Pin_4
  N7: S2.Pin_1, S2.Pin_2
  N8: S2.Pin_3, S2.Pin_4
